# Fritzing sketch schematic (saved by Fritzing 0.9.3b)
breadboards: 1

parts:
  Digispark1 = Digispark
  Part1 = ACS712 Low Current Sensor Board v12
  S1 = Round Pushbutton
  R1 = Resistor [tolerance=±5% resistance=430 package="1206 [SMD]"]
  I_used_relay_with_5V_power_input_and_digital_input_for_on/off = OMRON PCB Power Relay – G5LE [part_number="G5LE-1\n" package=THT]
  230V_input = Header 1 [package=1x01_offset]
  230V_output_for_Vacuum_cleaner = Header 1 [package=1x01_offset]
  JP3 = Header 1 [package=1x01_offset]
  JP4 = Header 1 [package=1x01_offset]
  230_output_for_Tool = Header 1 [package=1x01_offset]
  JP6 = Header 1 [package=1x01_offset]
  LED1 = smd LED [color="Red (633nm)" package="0603 [SMD]"]
  R3 = Resistor [tolerance=±5% resistance=10k package="1206 [SMD]"]

nets:
  VCC: Digispark1.VCC, Part1.5V, S1.leg0
  GND: Digispark1.GND, Part1.GND, I_used_relay_with_5V_power_input_and_digital_input_for_on/off.COIL2, LED1.cathode, R3.Pin_0
  N1: Digispark1.P0, R1.Pin_1, I_used_relay_with_5V_power_input_and_digital_input_for_on/off.COIL1
  N2: Digispark1.P1, S1.leg1, R3.Pin_1
  N3: Digispark1.P2, Part1.VO
  N4: Part1.IP+, I_used_relay_with_5V_power_input_and_digital_input_for_on/off.C, 230V_input.1
  N5: Part1.IP-, 230_output_for_Tool.1
  N6: R1.Pin_0, LED1.anode
  N7: I_used_relay_with_5V_power_input_and_digital_input_for_on/off.B, 230V_output_for_Vacuum_cleaner.1
  N8: JP3.1, JP4.1, JP6.1

custom parts:
  Digispark: The Digispark is an Attiny85 based microcontroller development board similar to the Arduino line, only cheaper, smaller, and a bit less powerful. With a whole host of shields to extend its functionality and the ability to use the familiar Arduino IDE the Digispark is a great way to jump into electronics, or perfect for when an Arduino is too big or too much.
